# Fritzing sketch ControlBoard (saved by Fritzing 0.9.6b)
breadboards: 1

parts:
  Part1 = Adafruit ESP32-S3 Feather [part_number="Adafruit #5323"]
  Adafruit_A4988_Stepper_Motor_Driver_Breakout1 = Adafruit A4988 Stepper Motor Driver Breakout [part_number=#6109]
  Adafruit_A4988_Stepper_Motor_Driver_Breakout2 = Adafruit A4988 Stepper Motor Driver Breakout [part_number=#6109]
  Part2 = Lithium Ion Polymer Battery 3.7v 350mAh [part_number=2750]

nets:
  GND: Part1.GND, Part1.A2, Adafruit_A4988_Stepper_Motor_Driver_Breakout1.GND, Adafruit_A4988_Stepper_Motor_Driver_Breakout2.GND, Part2.negative
  3.3V: Part1.3.3V, Adafruit_A4988_Stepper_Motor_Driver_Breakout1.VDD, Adafruit_A4988_Stepper_Motor_Driver_Breakout2.VDD
  5V: Part1.VBAT, Adafruit_A4988_Stepper_Motor_Driver_Breakout1.VMOTOR, Adafruit_A4988_Stepper_Motor_Driver_Breakout2.VMOTOR, Part2.positive
  CommonSLP: Part1.D11, Adafruit_A4988_Stepper_Motor_Driver_Breakout1.SLEEP, Adafruit_A4988_Stepper_Motor_Driver_Breakout2.SLEEP
  RearEN: Part1.D10, Adafruit_A4988_Stepper_Motor_Driver_Breakout1.ENABLE
  FrontEN: Part1.D9, Adafruit_A4988_Stepper_Motor_Driver_Breakout2.ENABLE
  CommonSTEP: Part1.D6, Adafruit_A4988_Stepper_Motor_Driver_Breakout1.STEP, Adafruit_A4988_Stepper_Motor_Driver_Breakout2.STEP
  CommonDIR: Part1.D5, Adafruit_A4988_Stepper_Motor_Driver_Breakout1.DIR, Adafruit_A4988_Stepper_Motor_Driver_Breakout2.DIR

custom parts:
  Adafruit ESP32-S3 Feather: The ESP32-S3 has arrived in Feather format - and what a great way to get started with this powerful new chip from Espressif! With dual 240 MHz cores, WiFi and BLE support, and native USB, this Feather is great for powering your IoT projects. That's right - it's the new Adafruit ESP32-S3 Feather! With native USB and 8 MB flash, this board will let you upgrade your existing ESP32 projects.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
  Adafruit A4988 Stepper Motor Driver Breakout: Stepper motors are used for CNC machines, 3D printers, and whenever else one needs precise, powerful motion. But to get good behavior from steppers you need a motor driver chip that can provide high bursts of current, and for smooth motion, be able to PWM that current for microstepping support. You can DIY this with a lot of timers, a microcontroller and an H-Bridge chip - or you could take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
  Lithium Ion Polymer Battery 3.7v 350mAh: Lithium ion polymer (also known as 'lipo' or 'lipoly') batteries are thin, light and powerful. The output ranges from 4.2V when completely charged to 3.7V. This battery has a capacity of 350mAh for a total of about 1.3 Wh. The batteries come pre-attached with a genuine 2-pin JST-PH connector as shown and include the necessary protection circuitry.
